# Fritzing sketch arduinocar電路圖專案 (saved by Fritzing 0.9.3b)

parts:
  S1 = H-Bridge with L298N
  元件1 = Arduino Uno (Rev3)
  VCC1 = 4 x AAA Battery Mount
  M1 = DC Motor
  M2 = DC Motor
  BT1 = Bluetooth HC-06u [package=THT]

nets:
  12V: S1.12V, 元件1.VIN, VCC1.+
  GND: S1.GND, 元件1.GND, VCC1.-, BT1.GND
  N1: S1.IN1, 元件1.D5_PWM
  N2: S1.IN2, 元件1.D6_PWM
  N3: S1.IN3, 元件1.D9_PWM
  N4: S1.IN4, 元件1.D10_PWM/SS
  N5: S1.OUT3-Motor2, M2.pin_2
  N6: S1.OUT4-Motor2, M2.pin_1
  N7: S1.OUT1-Motor1, M1.pin_1
  N8: S1.OUT2-Motor1, M1.pin_2
  N9: 元件1.D11_PWM/MOSI, BT1.TXD
  N10: 元件1.D12/MISO, BT1.RXD
  5V: 元件1.5V, BT1.VCC

custom parts:
  H-Bridge with L298N: h-bridge
  Bluetooth HC-06u: Bluetooth HC-06 - face up, pins down 16.5mm x 37.5mm PCB
